# Fritzing sketch CamLantern (saved by Fritzing 0.9.3b)
circuit board: 8.46667cm x 5.64444cm
breadboards: 1

parts:
  Part1 = Arduino Nano (Rev3.0)
  Part2 = NeoPixel Stick [part_number=1426]
  U1 = POT [package=pot_mammoth]
  U2 = POT [package=pot_mammoth]
  S1 = Pushbutton [package=THT]
  Power_plug1 = Power plug

nets:
  N1: Part1.D4, S1.leg0
  N2: Part1.D12/MISO, Part2.DATAIN
  N3: Part1.A7, U2.S
  N4: Part1.A6, U1.S
  +5V: Part2.+5V, U1.E, U2.E, Power_plug1.VCC
  GND: Part2.GND, U1.A, U2.A, S1.leg1, Power_plug1.GND

custom parts:
  NeoPixel Stick: Make your own little LED strip arrangement with this stick of NeoPixel LEDs. We crammed 8 of the tiny 5050 (5mm x 5mm) smart RGB LEDs onto a PCB with mounting holes and a chainable design. Use only one microcontroller pin to control as many as you can chain together! Each LED is addressable as the driver chip is inside the LED. Each one has ~18mA constant current drive so the color will be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
